# Fritzing sketch draft Sketch 1 (saved by Fritzing 0.9.3b)
breadboards: 1

parts:
  Part1 = Adafruit Feather nRF52 [part_number="Adafruit #3406"]
  U1 = Vibration Motor- ROB-08449 [package=vibe-motor-10mm]
  U2 = TRANSISTOR_NPN_2 [package=to-92]
  D1 = Diode [package=diode-1n4001]
  R1 = Resistor [tolerance=±5% resistance=220 package="0402 [SMD]"]
  SONAR1 = Maxbotix MaxSonar Ultrasonic Sensor (Hi-Res)

nets:
  3.3V: Part1.3.3V, U1.-, D1.C, SONAR1.+5V
  GND: Part1.GND, U2.C, SONAR1.GND
  N1: Part1.A5/0.29, SONAR1.AN
  N2: Part1.P0.11, R1.Pin_0
  N3: U1.+, U2.E, D1.A
  N4: U2.B, R1.Pin_1

custom parts:
  Maxbotix MaxSonar Ultrasonic Sensor (Hi-Res): Maxbotix MaxSonar Hi-Resolution Ultrasonic Sensor HRLV-EZ0, HRLV-EZ1, HRLV-EZ2, HRLV-EZ3, HRLV-EZ4

// code stored in the sketch: draft Sketch 1.ino
const int anPin = A5;
const int vMotor = 11;
long anVolt, mm, inches, pwm;

void setup() {
Serial.begin(9600);
// initialize digital pin LED_BUILTIN as an output.
pinMode(vMotor, OUTPUT);
}

void read_sensor(){
anVolt = analogRead(anPin);
mm = anVolt * 5;
inches = mm/25.4;
pwm = map(mm, 0,2500,200,50);
}

void print_range(){
Serial.print("S1");
Serial.print("=");
Serial.print(mm);
Serial.print("pwm");
Serial.print("=");
Serial.print(pwm);
Serial.print(" ");
Serial.println(inches);
}

void loop() {
read_sensor();
print_range();
analogWrite(vMotor, pwm);
//delay(20-(mm/200));
delay(100);
//digitalWrite(vMotor, LOW);
//delay(100);

}
